# Fritzing sketch Homekit LED Strip (saved by Fritzing 0.9.3b)
breadboards: 1

parts:
  U1 = Voltage Regulator [package=to220-adj]
  WeMos_D1_Mini1 = WeMos D1 Mini
  Q2 = Basic FET N-Channel [part_number=IRLB8721 package="TO220 [THT]"]
  Q1 = Basic FET N-Channel [part_number=IRLB8721 package="TO220 [THT]"]
  Q3 = Basic FET N-Channel [part_number=IRLB8721 package="TO220 [THT]"]
  S1 = Pushbutton [package=THT]

nets:
  N1: U1.IN, WeMos_D1_Mini1.3V3
  N2: U1.OUT, Q2.source, Q1.source, Q3.source
  N3: WeMos_D1_Mini1.D0, Q3.gate
  N4: WeMos_D1_Mini1.D1, S1.leg0
  N5: WeMos_D1_Mini1.D5, Q2.gate
  N6: WeMos_D1_Mini1.D6, Q1.gate
  N7: WeMos_D1_Mini1.G, S1.leg1

notes:
  12v in
  3.3v out
  (Goes through voltage regulator)
  Connection to LED Strip
  Manual On/Off Switch
